// Logisim project Ctl_Data_Processing.circ as structural Verilog: 1 circuit, main circuit Data_Processing
module Data_Processing (
  input  [15:0] Instruction,
  input  Enable,
  output [3:0] ALU_Opcode,
  output [2:0] Rd,
  output [2:0] Rn,
  output [2:0] Rm,
  output [3:0] Flags_Update_Mask,
  output [3:0] out_8
);

  wire and_2_out, and_3_out, and_4_out, and_5_out, and_6_out, not_1_out, not_2_out, not_3_out, not_4_out;
  wire [2:0] BITS_345;
  wire [3:0] bit_extender_2_out;
  wire [15:0] bit_extender_1_out;
  wire [15:10] and_1_out;

  assign bit_extender_1_out = {{15{Enable}}, Enable};  // Bit_Extender bit_extender_1
  assign {and_1_out, ALU_Opcode, BITS_345, Rd} = Instruction & bit_extender_1_out;  // AND_Gate and_1, 16 bits wide
  Multiplexer #(.enable("false"), .select(4), .width(3)) multiplexer_1 (
    .in0(Rd), .in1(Rd), .in2(Rd), .in3(Rd), .in4(Rd), .in5(Rd), .in6(Rd), .in7(Rd), .in8(Rd), .in9(BITS_345),
    .in10(Rd), .in11(Rd), .in12(Rd), .in13(BITS_345), .in14(Rd), .in15(Rd), .out(Rn), .sel(ALU_Opcode));
  Multiplexer #(.enable("false"), .select(4), .width(3)) multiplexer_2 (
    .in0(BITS_345), .in1(BITS_345), .in2(BITS_345), .in3(BITS_345), .in4(BITS_345), .in5(BITS_345),
    .in6(BITS_345), .in7(BITS_345), .in8(BITS_345), .in9(BITS_345), .in10(BITS_345), .in11(BITS_345),
    .in12(BITS_345), .in13(Rd), .in14(BITS_345), .in15(BITS_345), .out(Rm), .sel(ALU_Opcode));
  not not_1 (not_1_out, ALU_Opcode[3]);
  not not_2 (not_2_out, ALU_Opcode[2]);
  not not_3 (not_3_out, ALU_Opcode[1]);
  not not_4 (not_4_out, ALU_Opcode[0]);
  or or_1 (out_8[1], ALU_Opcode[1], not_4_out, not_2_out, not_1_out);
  and and_2 (and_2_out, not_1_out, ALU_Opcode[2], not_3_out, ALU_Opcode[0]);
  and and_3 (and_3_out, not_1_out, ALU_Opcode[2], ALU_Opcode[1], not_4_out);
  and and_4 (and_4_out, ALU_Opcode[3], not_2_out, not_3_out, ALU_Opcode[0]);
  or or_2 (out_8[0], and_2_out, and_3_out, and_4_out, and_5_out, and_6_out);
  and and_5 (and_5_out, ALU_Opcode[3], not_2_out, ALU_Opcode[1], not_4_out);
  and and_6 (and_6_out, ALU_Opcode[3], not_2_out, ALU_Opcode[1], ALU_Opcode[0]);
  assign bit_extender_2_out = {{3{Enable}}, Enable};  // Bit_Extender bit_extender_2
  assign Flags_Update_Mask = bit_extender_2_out & {2'b11, out_8[1:0]};  // AND_Gate and_7, 4 bits wide

  assign out_8[3:2] = 2'b11;

  // Other names for the same wires on the sheet: BITS_012[2:0] = Rd

  // Notes on the sheet:
  //   Note 2: RSB instruction has Rn as 1st operand.
  //   MUL instruction has Rn as 1st operand and Rdm as 2nd operand
  //   For simplification purposes, Rm is used for 1st operand both here and in the ALU.
  //   Note: instructions that does not save the result will still have the second operand as the destination register, the ALU will copy the second register to the destination register
  //   Pull output low on Enable = 0
endmodule
