// Logisim project Ctl_Load_Store.circ as structural Verilog: 1 circuit, main circuit Load_Store
module Load_Store (
  input  Enable,
  input  [15:0] Instruction,
  input  Clk,
  input  Reset,
  input  [31:0] Stack_Pointer,
  output Load,
  output PC_Hold,
  output [2:0] Rmd,
  output Store,
  output [31:0] RAM_Addr
);

  wire and_4_out, d_ff_1_q, d_ff_1_qn, not_1_out, not_2_out;
  wire [2:0] bit_extender_2_out;
  wire [31:0] bit_extender_1_out, bit_extender_3_out, IMM8_plus_SP;

  assign bit_extender_1_out = {{24{Instruction[7]}}, Instruction[7:0]};  // Bit_Extender bit_extender_1
  Adder #(.width(32)) adder_1 (.a(bit_extender_1_out), .b(Stack_Pointer), .out(IMM8_plus_SP));  // open: cin, cout
  assign bit_extender_2_out = {{2{Enable}}, Enable};  // Bit_Extender bit_extender_2
  assign bit_extender_3_out = {{31{Enable}}, Enable};  // Bit_Extender bit_extender_3
  assign Rmd = Instruction[10:8] & bit_extender_2_out;  // AND_Gate and_1, 3 bits wide
  and and_2 (Store, Enable, ~Instruction[11]);  // AND_Gate
  assign RAM_Addr = bit_extender_3_out & ~IMM8_plus_SP;  // AND_Gate and_3, 32 bits wide
  and and_4 (and_4_out, ~d_ff_1_q, Instruction[11]);  // AND_Gate
  D_Flip_Flop d_ff_1 (.D(and_4_out), .clk(Clk), .Q(d_ff_1_q), .Qn(d_ff_1_qn));  // open: preset, reset
  // OR_Gate or_1 has open pins: in0=not_1_out, in1=not_2_out, in2=Reset, out=open
  not not_1 (not_1_out, Instruction[11]);
  not not_2 (not_2_out, Enable);
  and and_5 (Load, Enable, Instruction[11], d_ff_1_q);
  and and_6 (PC_Hold, Instruction[11], d_ff_1_qn, Enable);

  // Other names for the same wires on the sheet: IMM8[7:0] = Instruction[7:0]; RT[2:0] = Instruction[10:8];
  //   Instru = Instruction[11]

  // Notes on the sheet:
  //   Instruction: pull=down
  //   Delay load and hold PC for 1 cycle for the RAM to send out requested data 
endmodule
