// Logisim project Ctl_Shift_Add_Sub_Mov.circ as structural Verilog: 1 circuit, main circuit Shift_Add_Sub_Mov
module Shift_Add_Sub_Mov (
  input  Enable,
  input  [15:0] Instruction,
  output [2:0] Rm,
  output Carry,
  output [2:0] Rn,
  output Imm32_Enable,
  output [2:0] Rd,
  output [31:0] Imm32,
  output [4:0] Imm5,
  output [3:0] Flags_Update_Mask,
  output [3:0] ALU_Opcode
);

  wire ADD_IMM, add_imm_t, ADD_REG, add_reg_t, and_1_out, and_2_out, and_9_out, and_10_out, and_11_out,
       and_12_out, and_13_out, and_14_out, and_16_out, and_17_out, and_18_out, and_19_out, and_20_out, ASR,
       CMP, LSL, LSR, MOV, not_1_out, not_2_out, not_3_out, not_4_out, not_5_out, or_1_out, or_2_out,
       or_3_out, or_4_out, or_5_out, or_13_out, or_14_out, SUB, sub_imm, sub_reg;
  wire [1:0] or_15_out;
  wire [2:0] IMM3, RD_2, RD_3, RD_4, RD_t, RDN_4, RM_2, RM_t, RN_2, RN_3;
  wire [3:0] bit_extender_9_out, bit_extender_10_out, or_7_out;
  wire [7:0] IMM8;
  wire [15:0] and_5_out, and_6_out, bit_extender_1_out, bit_extender_2_out, bit_extender_3_out,
       bit_extender_4_out, bit_extender_5_out, bit_extender_6_out, Instru;
  wire [15:9] and_7_out, and_8_out;
  wire [15:11] and_4_out;
  wire [31:0] bit_extender_7_out, bit_extender_8_out, multiplexer_1_out, negator_1_out;

  or or_1 (or_1_out, LSL, LSR, ASR);
  Decoder #(.select(2)) decoder_1 (
    .out0(add_reg_t), .out1(sub_reg), .out2(add_imm_t), .out3(sub_imm), .sel(Instru[10:9]));  // open: en
  or or_2 (or_2_out, add_reg_t, sub_reg);
  or or_3 (or_3_out, add_imm_t, sub_imm);
  or or_4 (or_4_out, MOV, CMP);
  or or_5 (or_5_out, ADD_IMM, SUB);
  assign bit_extender_1_out = {{15{Enable}}, Enable};  // Bit_Extender bit_extender_1
  Decoder #(.select(3)) decoder_2 (
    .out0(LSL), .out1(LSR), .out2(ASR), .out3(ADD_REG), .out4(MOV), .out5(CMP), .out6(ADD_IMM), .out7(SUB),
    .sel(Instru[13:11]));  // open: en
  assign bit_extender_2_out = {{15{or_1_out}}, or_1_out};  // Bit_Extender bit_extender_2
  and and_1 (and_1_out, ADD_REG, or_2_out);
  and and_2 (and_2_out, ADD_REG, or_3_out);
  assign bit_extender_3_out = {{15{or_4_out}}, or_4_out};  // Bit_Extender bit_extender_3
  assign bit_extender_4_out = {{15{or_5_out}}, or_5_out};  // Bit_Extender bit_extender_4
  assign Instru = Instruction & bit_extender_1_out;  // AND_Gate and_3, 16 bits wide
  assign {and_4_out, Imm5, RM_t, RD_t} = bit_extender_2_out & Instru;  // AND_Gate and_4, 16 bits wide
  assign bit_extender_5_out = {{15{and_1_out}}, and_1_out};  // Bit_Extender bit_extender_5
  assign bit_extender_6_out = {{15{and_2_out}}, and_2_out};  // Bit_Extender bit_extender_6
  assign {and_5_out[15:11], RD_4, and_5_out[7:0]} = bit_extender_3_out & Instru;  // AND_Gate and_5, 16 bits wide
  assign {and_6_out[15:11], RDN_4, and_6_out[7:0]} = bit_extender_4_out & Instru;  // AND_Gate and_6, 16 bits wide
  assign {and_7_out, RM_2, RN_2, RD_2} = bit_extender_5_out & Instru;  // AND_Gate and_7, 16 bits wide
  assign {and_8_out, IMM3, RN_3, RD_3} = bit_extender_6_out & Instru;  // AND_Gate and_8, 16 bits wide
  assign IMM8 = and_5_out[7:0] | and_6_out[7:0];  // OR_Gate or_6, 8 bits wide
  not not_1 (not_1_out, Instru[13]);
  not not_2 (not_2_out, Instru[12]);
  not not_3 (not_3_out, Instru[11]);
  not not_4 (not_4_out, Instru[9]);
  and and_9 (and_9_out, not_1_out, Instru[11], not_4_out);
  and and_10 (and_10_out, not_3_out, Instru[13]);
  or or_7 (or_7_out[0], and_9_out, and_10_out, and_11_out);
  assign bit_extender_7_out = {{24{1'b0}}, IMM8};  // Bit_Extender bit_extender_7
  and and_11 (and_11_out, Instru[11], not_2_out, not_1_out);
  assign bit_extender_8_out = {{29{1'b0}}, IMM3};  // Bit_Extender bit_extender_8
  Negator #(.width(32)) negator_1 (.in(bit_extender_7_out), .out(negator_1_out));
  assign Rn = RN_2 | RDN_4 | RM_t | RN_3;  // OR_Gate or_8, 3 bits wide
  Multiplexer #(.enable("false"), .width(32)) multiplexer_1 (
    .in0(bit_extender_7_out), .in1(negator_1_out), .out(multiplexer_1_out), .sel(MOV));
  and and_12 (and_12_out, Instru[13], Instru[11]);
  assign Rm = RM_t | RM_2;  // OR_Gate or_9, 3 bits wide
  assign Imm32 = bit_extender_8_out | multiplexer_1_out;  // OR_Gate or_10, 32 bits wide
  and and_13 (and_13_out, Instru[9], Instru[11]);
  or or_11 (or_7_out[1], and_12_out, and_13_out, and_14_out);
  assign Rd = RD_t | RD_3 | RD_2 | RD_4 | RDN_4;  // OR_Gate or_12, 3 bits wide
  and and_14 (and_14_out, not_1_out, not_2_out);
  and and_15 (or_7_out[3], not_2_out, Instru[13]);
  or or_13 (or_13_out, add_imm_t, sub_imm);
  or or_14 (or_14_out, sub_reg, sub_imm);
  and and_16 (and_16_out, Instru[11], Instru[12]);
  and and_17 (and_17_out, or_14_out, ADD_REG);
  and and_18 (and_18_out, ADD_REG, or_13_out);
  and and_19 (and_19_out, Instru[13], Instru[12]);
  or or_15 (or_15_out[0], and_16_out, and_19_out, and_20_out);
  or or_16 (Carry, SUB, and_17_out);
  or or_17 (Imm32_Enable, MOV, CMP, ADD_IMM, SUB, and_18_out);
  and and_20 (and_20_out, Instru[13], Instru[11]);
  assign bit_extender_9_out = {{3{Enable}}, Enable};  // Bit_Extender bit_extender_9
  assign ALU_Opcode = bit_extender_9_out & {or_7_out[3], Instru[12], or_7_out[1:0]};  // AND_Gate and_21, 4 bits wide
  not not_5 (not_5_out, Instru[13]);
  or or_18 (or_15_out[1], not_5_out, Instru[12], Instru[11]);
  assign bit_extender_10_out = {{3{Enable}}, Enable};  // Bit_Extender bit_extender_10
  assign Flags_Update_Mask = bit_extender_10_out & {2'b11, or_15_out};  // AND_Gate and_22, 4 bits wide

  // Notes on the sheet:
  //   Pull output low on Enable = 0
  //   Enable carry for SUB since it is reversed in ALU
  //   only ADD and SUB use Rm
  //   ALU will use Imm32 instead of Rm
endmodule
