// Logisim project Processeur.circ as structural Verilog: 1 circuit, main circuit main
module main (
  input  [15:0] Instruction,
  input  CLK,
  input  RST
);

  wire banc_de_registre_1_p1, UAL_Cin;
  wire [3:0] flags, UAL_opcode;
  wire [31:0] banc_de_registre_1_p4, banc_de_registre_1_p5;

  Controller controller_1 (
    .ALU_Opcode(UAL_opcode), .Carry(UAL_Cin), .FlagsIn(flags), .Clk(CLK), .Reset(RST), .Inst(Instruction));  // open: DP_Shift, Imm32_Enable, Imm5, Imm32, Rm, Rn, Rd, Flags, RAM_Addr, Load, Store, SP, PC
  // banc_de_registre banc_de_registre_1: pin names not known; wires that end beside it: banc_de_registre_1_p1, RST, CLK, banc_de_registre_1_p4, banc_de_registre_1_p5
  UAL ual_1 (
    .A(banc_de_registre_1_p4), .Cin(UAL_Cin), .B(banc_de_registre_1_p5), .Codop(UAL_opcode));  // open: Shift, s
endmodule
