// Logisim project TD1.circ as structural Verilog
module UAL (
  input  [4:0] Shift,
  input  [31:0] A,
  input  Cin,
  input  [31:0] B,
  input  [3:0] Codop,
  input  [31:0] s
);

  wire negator_1_out;
  wire [31:0] I_ADC, I_AND, I_ASR, I_BIC, I_CMN, I_CMP, I_EOR, I_LSL, I_LSR, I_MUL, I_MVN, I_ORR, I_ROR,
       I_RSB, I_SBC, I_XOR;

  assign I_MVN = ~A;  // NOT_Gate not_1, 32 bits wide
  Shifter #(.width(32)) shifter_1 (.in(B), .\dist (Shift), .out(I_LSL));
  Shifter #(.shift("lr"), .width(32)) shifter_2 (.in(B), .\dist (Shift), .out(I_LSR));
  Shifter #(.shift("ar"), .width(32)) shifter_3 (.in(B), .\dist (Shift), .out(I_ASR));
  Shifter #(.shift("rr"), .width(32)) shifter_4 (.in(B), .\dist (Shift), .out(I_ROR));
  assign I_AND = A & B;  // AND_Gate and_1, 32 bits wide
  assign I_XOR = A ^ B;  // XOR_Gate xor_1, 32 bits wide
  assign I_ORR = A | B;  // OR_Gate or_1, 32 bits wide
  assign I_BIC = B & I_MVN;  // AND_Gate and_2, 32 bits wide
  Adder #(.width(32)) adder_1 (.a(A), .b(B), .out(I_ADC), .cin(Cin));  // open: cout
  Negator #(.width(1)) negator_1 (.in(Cin), .out(negator_1_out));
  Negator #(.width(32)) negator_2 (.in(A), .out(I_RSB));
  Subtractor #(.width(32)) subtractor_1 (.a(B), .b(A), .out(I_CMP));  // open: bin, bout
  Adder #(.width(32)) adder_2 (.a(A), .b(B), .out(I_CMN));  // open: cin, cout
  Multiplier #(.width(32)) multiplier_1 (.a(A), .b(B), .out(I_MUL));  // open: cin, cout
  Subtractor #(.width(32)) subtractor_2 (.a(B), .b(A), .out(I_SBC), .bin(negator_1_out));  // open: bout
  Multiplexer #(.enable("false"), .select(4), .width(32)) multiplexer_1 (
    .in0(I_AND), .in1(I_EOR), .in2(I_LSL), .in3(I_LSR), .in4(I_ASR), .in5(I_ADC), .in6(I_SBC), .in7(I_ROR),
    .in9(I_RSB), .in10(I_CMP), .in11(I_CMN), .in12(I_ORR), .in13(I_MUL), .in14(I_BIC), .in15(I_MVN), .out(s),
    .sel(Codop));  // open: in8
endmodule
