// Logisim project ALU.circ as structural Verilog
module UAL (
  input  [4:0] Shift,
  input  [31:0] A,
  input  Cin,
  input  [31:0] B,
  input  [3:0] Codop,
  input  [31:0] s,
  input  [3:0] Flags
);

  wire adder_2_cout, flag_C_ADC, flag_C_ASR, flag_C_CMN, flag_C_CMP, flag_C_LSL, flag_C_LSR, flag_C_MUL,
       flag_C_RSD, flag_C_SBC, flag_V_ADC, flag_V_CMN, flag_V_CMP, flag_V_SBC, negator_1_out,
       subtractor_1_bout, subtractor_2_bout, xnor_1_out, xnor_2_out, xor_2_out, xor_3_out, xor_4_out,
       xor_5_out, xor_6_out, xor_7_out;
  wire [4:0] negator_3_out, subtractor_3_out, subtractor_4_out;
  wire [31:0] CMN_F_ENTREE, CMP_F_ENTREE, I_ADC, I_AND, I_ASR, I_BIC, I_EOR, I_LSL, I_LSR, I_MUL, I_MVN,
       I_ORR, I_ROR, I_RSB, I_SBC, I_XOR, multiplexer_4_out, TST_F_ENTREE;

  Adder #(.width(32)) adder_1 (.a(A), .b(B), .out(I_ADC), .cin(Cin), .cout(flag_C_ADC));
  Negator #(.width(1)) negator_1 (.in(Cin), .out(negator_1_out));
  Negator #(.width(32)) negator_2 (.in(A), .out(I_RSB));
  Subtractor #(.width(32)) subtractor_1 (.a(B), .b(A), .out(CMP_F_ENTREE), .bout(subtractor_1_bout));  // open: bin
  Adder #(.width(32)) adder_2 (.a(A), .b(B), .out(CMN_F_ENTREE), .cout(adder_2_cout));  // open: cin
  Multiplier #(.width(32)) multiplier_1 (.a(A), .b(B), .out(I_MUL));  // open: cin, cout
  assign I_MVN = ~A;  // NOT_Gate not_1, 32 bits wide
  assign TST_F_ENTREE = A & B;  // AND_Gate and_1, 32 bits wide
  assign I_AND = A & B;  // AND_Gate and_2, 32 bits wide
  assign I_XOR = A ^ B;  // XOR_Gate xor_1, 32 bits wide
  assign I_ORR = A | B;  // OR_Gate or_1, 32 bits wide
  assign I_BIC = B & I_MVN;  // AND_Gate and_3, 32 bits wide
  Shifter #(.width(32)) shifter_1 (.in(B), .\dist (Shift), .out(I_LSL));
  Shifter #(.shift("lr"), .width(32)) shifter_2 (.in(B), .\dist (Shift), .out(I_LSR));
  Shifter #(.shift("ar"), .width(32)) shifter_3 (.in(B), .\dist (Shift), .out(I_ASR));
  Shifter #(.shift("rr"), .width(32)) shifter_4 (.in(B), .\dist (Shift), .out(I_ROR));
  Subtractor #(.width(32)) subtractor_2 (.a(B), .b(A), .out(I_SBC), .bin(negator_1_out), .bout(subtractor_2_bout));
  not not_2 (flag_C_SBC, subtractor_2_bout);
  not not_3 (flag_C_CMN, adder_2_cout);
  BitSelector #(.width(32)) bitselector_1 (.in(B), .out(flag_C_LSL), .sel(negator_3_out));
  Negator #(.width(5)) negator_3 (.in(Shift), .out(negator_3_out));
  BitSelector #(.width(32)) bitselector_2 (.in(B), .out(flag_C_LSR), .sel(subtractor_3_out));
  Subtractor #(.width(5)) subtractor_3 (.a(Shift), .b(5'b00001), .out(subtractor_3_out));  // open: bin, bout
  not not_4 (flag_C_CMP, subtractor_1_bout);
  xor xor_2 (xor_2_out, B[31], s[31]);
  xnor xnor_1 (xnor_1_out, A[31], B[31]);
  and and_4 (flag_V_ADC, xor_2_out, xnor_1_out);
  xor xor_3 (xor_3_out, B[31], s[31]);
  xor xor_4 (xor_4_out, A[31], B[31]);
  BitSelector #(.width(32)) bitselector_3 (.in(B), .out(flag_C_ASR), .sel(subtractor_4_out));
  Subtractor #(.width(5)) subtractor_4 (.a(Shift), .b(5'b00001), .out(subtractor_4_out));  // open: bin, bout
  and and_5 (flag_V_SBC, xor_3_out, xor_4_out);
  xor xor_5 (xor_5_out, B[31], CMP_F_ENTREE[31]);
  xor xor_6 (xor_6_out, A[31], B[31]);
  and and_6 (flag_V_CMP, xor_5_out, xor_6_out);
  xor xor_7 (xor_7_out, B[31], CMN_F_ENTREE[31]);
  xnor xnor_2 (xnor_2_out, A[31], B[31]);
  Multiplexer #(.enable("false"), .select(4), .width(32)) multiplexer_1 (
    .in0(I_AND), .in1(I_EOR), .in2(I_LSL), .in3(I_LSR), .in4(I_ASR), .in5(I_ADC), .in6(I_SBC), .in7(I_ROR),
    .in8(B), .in9(I_RSB), .in10(B), .in11(B), .in12(I_ORR), .in13(I_MUL), .in14(I_BIC), .in15(I_MVN),
    .out(s), .sel(Codop));
  and and_7 (flag_V_CMN, xor_7_out, xnor_2_out);
  Multiplexer #(.enable("false"), .select(4)) multiplexer_2 (
    .in0(1'b0), .in1(1'b0), .in2(flag_C_LSL), .in3(flag_C_LSR), .in4(flag_C_ASR), .in5(flag_C_ADC),
    .in6(flag_C_SBC), .in7(Flags[3]), .in8(1'b0), .in9(flag_C_RSD), .in10(flag_C_CMP), .in11(flag_C_CMN),
    .in12(1'b0), .in13(flag_C_MUL), .in14(1'b0), .in15(1'b0), .out(Flags[1]), .sel(Codop));
  Multiplexer #(.enable("false"), .select(4)) multiplexer_3 (
    .in0(1'b0), .in1(1'b0), .in2(1'b0), .in3(1'b0), .in4(1'b0), .in5(flag_V_ADC), .in6(flag_V_SBC),
    .in7(1'b0), .in8(1'b0), .in9(1'b0), .in10(flag_V_CMP), .in11(flag_V_CMN), .in12(1'b0), .in13(1'b0),
    .in14(1'b0), .in15(1'b0), .out(Flags[0]), .sel(Codop));
  Multiplexer #(.enable("false"), .select(4), .width(32)) multiplexer_4 (
    .in0(s), .in1(s), .in2(s), .in3(s), .in4(s), .in5(s), .in6(s), .in7(s), .in8(TST_F_ENTREE), .in9(s),
    .in10(CMP_F_ENTREE), .in11(CMN_F_ENTREE), .in12(s), .in13(s), .in14(s), .in15(s),
    .out(multiplexer_4_out), .sel(Codop));
  Comparator #(.width(32)) comparator_1 (
    .a(multiplexer_4_out), .b({32{1'b0}}), .eq(Flags[2]), .lt(Flags[3]));  // open: gt

  // Other names for the same wires on the sheet: flag_V = Flags[0]; flag_C = Flags[1]; flag_Z = Flags[2];
  //   flag_C_ROR = Flags[3]; flag_N = Flags[3]; I_CMN[31:0] = B; I_CMP[31:0] = B; I_TST[31:0] = B
endmodule
