// Logisim project BancDeRegistres.circ as structural Verilog: 1 circuit, main circuit BancRegistre
module BancRegistre (
  input  [2:0] RegDest,
  input  [31:0] DataIn,
  input  Reset,
  input  Clk,
  input  [2:0] RegA,
  input  [2:0] RegB,
  input  [31:0] in_7,
  output [31:0] Aout,
  output [31:0] R_0,
  output [31:0] R_1,
  output [31:0] R_2,
  output [31:0] R_3,
  output [31:0] R_4,
  output [31:0] R_5,
  output [31:0] R_6,
  output [31:0] R_7,
  output [31:0] Bout
);

  wire demultiplexer_1_out0, demultiplexer_1_out1, demultiplexer_1_out2, demultiplexer_1_out3,
       demultiplexer_1_out4, demultiplexer_1_out5, demultiplexer_1_out6, demultiplexer_1_out7;

  Demultiplexer #(.enable("false"), .select(3)) demultiplexer_1 (
    .out0(demultiplexer_1_out0), .out1(demultiplexer_1_out1), .out2(demultiplexer_1_out2),
    .out3(demultiplexer_1_out3), .out4(demultiplexer_1_out4), .out5(demultiplexer_1_out5),
    .out6(demultiplexer_1_out6), .out7(demultiplexer_1_out7), .in(1'b1), .sel(RegDest));
  Register #(.width(32)) R0 (.D(DataIn), .en(demultiplexer_1_out0), .clk(Clk), .Q(R_0), .clr(Reset));
  Register #(.width(32)) R1 (.D(DataIn), .en(demultiplexer_1_out1), .clk(Clk), .Q(R_1), .clr(Reset));
  Register #(.width(32)) R2 (.D(DataIn), .en(demultiplexer_1_out2), .clk(Clk), .Q(R_2), .clr(Reset));
  Register #(.width(32)) R3 (.D(DataIn), .en(demultiplexer_1_out3), .clk(Clk), .Q(R_3), .clr(Reset));
  Register #(.width(32)) R4 (.D(DataIn), .en(demultiplexer_1_out4), .clk(Clk), .Q(R_4), .clr(Reset));
  Register #(.width(32)) R5 (.D(DataIn), .en(demultiplexer_1_out5), .clk(Clk), .Q(R_5), .clr(Reset));
  Register #(.width(32)) R6 (.D(DataIn), .en(demultiplexer_1_out6), .clk(Clk), .Q(R_6), .clr(Reset));
  Register #(.width(32)) R7 (.D(DataIn), .en(demultiplexer_1_out7), .clk(Clk), .Q(R_7), .clr(Reset));
  Multiplexer #(.enable("false"), .select(3), .width(32)) multiplexer_1 (
    .in0(R_0), .in1(R_1), .in2(R_2), .in3(R_3), .in4(R_4), .in5(R_5), .in6(R_6), .in7(R_7), .out(Aout),
    .sel(RegA));
  Multiplexer #(.enable("false"), .select(3), .width(32)) multiplexer_2 (
    .in0(R_0), .in1(R_1), .in2(R_2), .in3(R_3), .in4(R_4), .in5(R_5), .in6(R_6), .in7(R_7), .out(Bout),
    .sel(RegB));
endmodule
