// Logisim project Ctl_Conditional.circ as structural Verilog: 1 circuit, main circuit Conditional
module Conditional (
  input  Enable,
  input  [15:0] Instruction,
  input  Z,
  input  C,
  input  N,
  input  V,
  output [10:0] Offset,
  output Verified
);

  wire multiplexer_3_out, o2, o4, o6, o8, o9, o10, o11, o12, o13, o14, or_2_out, xnor_1_out, xor_1_out;
  wire [10:0] multiplexer_1_out;

  xnor xnor_1 (xnor_1_out, N, V);
  xor xor_1 (xor_1_out, N, V);
  not not_1 (o2, Z);
  not not_2 (o4, C);
  not not_3 (o6, N);
  not not_4 (o8, V);
  and and_1 (o9, ~Z, C);  // AND_Gate
  and and_2 (o10, Z, ~C);  // AND_Gate
  xnor xnor_2 (o11, N, V);
  xor xor_2 (o12, N, V);
  and and_3 (o13, xnor_1_out, ~Z);  // AND_Gate
  or or_1 (o14, xor_1_out, Z);
  Multiplexer #(.enable("false"), .width(11)) multiplexer_1 (
    .in0({3'b000, Instruction[7:0]}), .in1(Instruction[10:0]), .out(multiplexer_1_out), .sel(Instruction[13]));
  Multiplexer #(.enable("false"), .width(11)) multiplexer_2 (
    .in0({11{1'b0}}), .in1(multiplexer_1_out), .out(Offset), .sel(Verified));
  Multiplexer #(.enable("false"), .select(4)) multiplexer_3 (
    .in0(Z), .in1(o2), .in2(C), .in3(o4), .in4(N), .in5(o6), .in6(V), .in7(o8), .in8(o9), .in9(o10),
    .in10(o11), .in11(o12), .in12(o13), .in13(o14), .in14(1'b1), .in15(1'b0), .out(multiplexer_3_out),
    .sel(Instruction[11:8]));
  or or_2 (or_2_out, Instruction[13], multiplexer_3_out);
  and and_4 (Verified, Enable, or_2_out);

  // Other names for the same wires on the sheet: imm8[7:0] = Instruction[7:0]; imm11[10:0] = Instruction[10:0];
  //   condition[3:0] = Instruction[11:8]; unconditional = Instruction[13]; o1 = Z; o3 = C; o5 = N; o7 = V
endmodule
