// Logisim project Ctl_SP_Address.circ as structural Verilog: 1 circuit, main circuit SP_Address
module SP_Address (
  input  [31:0] Stack_Pointer,
  input  [15:0] Instruction,
  input  Enable,
  output [31:0] New_Stack_Pointer,
  output Write_Enable
);

  wire INSTRU;
  wire [6:0] IMM7;
  wire [15:0] bit_extender_1_out;
  wire [15:8] and_1_out;
  wire [31:0] ADDITION, bit_extender_2_out, bit_extender_3_out, bit_extender_4_out, New_Stack_Pointer_t,
       SOUSTRACTION;

  assign bit_extender_1_out = {{15{Enable}}, Enable};  // Bit_Extender bit_extender_1
  assign bit_extender_2_out = {{25{1'b0}}, IMM7};  // Bit_Extender bit_extender_2
  assign bit_extender_3_out = {{25{1'b0}}, IMM7};  // Bit_Extender bit_extender_3
  assign {and_1_out, INSTRU, IMM7} = Instruction & bit_extender_1_out;  // AND_Gate and_1, 16 bits wide
  Adder #(.width(32)) adder_1 (.a(Stack_Pointer), .b(bit_extender_2_out), .out(ADDITION));  // open: cin, cout
  Subtractor #(.width(32)) subtractor_1 (
    .a(Stack_Pointer), .b(bit_extender_3_out), .out(SOUSTRACTION));  // open: bin, bout
  assign bit_extender_4_out = {{31{Enable}}, Enable};  // Bit_Extender bit_extender_4
  assign New_Stack_Pointer = New_Stack_Pointer_t & bit_extender_4_out;  // AND_Gate and_2, 32 bits wide
  Multiplexer #(.enable("false"), .width(32)) multiplexer_1 (
    .in0(ADDITION), .in1(SOUSTRACTION), .out(New_Stack_Pointer_t), .sel(INSTRU));

  assign Write_Enable = Enable;

  // Notes on the sheet:
  //   Pull output low on Enable = 0
endmodule
