// Logisim project Ctl_Shift_Add_Sub_Mov.circ as structural Verilog: 2 circuits, main circuit Shift_Add_Sub_Mov
module Shift_Add_Sub_Mov (
  input  Enable,
  input  [15:0] Instruction,
  output [3:0] Flags_Update_Mask,
  output Carry,
  output Imm32_Enable,
  output [2:0] Rm,
  output [2:0] Rn,
  output [2:0] Rd,
  output [4:0] Imm5,
  output [31:0] Imm32,
  output [3:0] ALU_Opcode
);

  wire ADD_IMM, add_imm_t, ADD_REG, add_reg_t, and_2_out, and_5_out, and_6_out, and_10_out, and_11_out,
       and_12_out, and_13_out, and_14_out, and_16_out, and_17_out, ASR, CMP, LSL, LSR, MOV, not_1_out,
       not_2_out, not_3_out, not_4_out, or_1_out, or_2_out, or_3_out, or_4_out, or_5_out, or_6_out, or_8_out,
       SUB, sub_imm, sub_reg;
  wire [2:0] IMM3, RD_2, RD_3, RD_4, RD_t, RDN_4, RM_2, RM_t, RN_2, RN_3;
  wire [3:0] bit_extender_9_out, bit_extender_10_out, flag_update_1_flags_update_mask, or_11_out;
  wire [7:0] IMM8;
  wire [15:0] and_3_out, and_7_out, bit_extender_1_out, bit_extender_2_out, bit_extender_3_out,
       bit_extender_4_out, bit_extender_5_out, bit_extender_6_out, Instru;
  wire [15:9] and_8_out, and_9_out;
  wire [15:11] and_4_out;
  wire [31:0] bit_extender_7_out, bit_extender_8_out, multiplexer_1_out, negator_1_out;

  or or_1 (or_1_out, MOV, CMP);
  or or_2 (or_2_out, ADD_IMM, SUB);
  assign bit_extender_1_out = {{15{Enable}}, Enable};  // Bit_Extender bit_extender_1
  or or_3 (or_3_out, LSL, LSR, ASR);
  or or_4 (or_4_out, add_reg_t, sub_reg);
  or or_5 (or_5_out, add_imm_t, sub_imm);
  assign bit_extender_2_out = {{15{or_1_out}}, or_1_out};  // Bit_Extender bit_extender_2
  assign bit_extender_3_out = {{15{or_2_out}}, or_2_out};  // Bit_Extender bit_extender_3
  assign Instru = Instruction & bit_extender_1_out;  // AND_Gate and_1, 16 bits wide
  Decoder #(.select(3)) decoder_1 (
    .out0(LSL), .out1(LSR), .out2(ASR), .out3(ADD_REG), .out4(MOV), .out5(CMP), .out6(ADD_IMM), .out7(SUB),
    .sel(Instru[13:11]));  // open: en
  assign bit_extender_4_out = {{15{or_3_out}}, or_3_out};  // Bit_Extender bit_extender_4
  Decoder #(.select(2)) decoder_2 (
    .out0(add_reg_t), .out1(sub_reg), .out2(add_imm_t), .out3(sub_imm), .sel(Instru[10:9]));  // open: en
  or or_6 (or_6_out, add_imm_t, sub_imm);
  and and_2 (and_2_out, ADD_REG, or_5_out);
  assign {and_3_out[15:11], RD_4, and_3_out[7:0]} = bit_extender_2_out & Instru;  // AND_Gate and_3, 16 bits wide
  assign {and_4_out, Imm5, RM_t, RD_t} = bit_extender_4_out & Instru;  // AND_Gate and_4, 16 bits wide
  and and_5 (and_5_out, ADD_REG, or_4_out);
  and and_6 (and_6_out, ADD_REG, or_6_out);
  or or_7 (Imm32_Enable, MOV, CMP, ADD_IMM, SUB, and_2_out);
  assign {and_7_out[15:11], RDN_4, and_7_out[7:0]} = bit_extender_3_out & Instru;  // AND_Gate and_7, 16 bits wide
  assign bit_extender_5_out = {{15{and_5_out}}, and_5_out};  // Bit_Extender bit_extender_5
  assign bit_extender_6_out = {{15{and_6_out}}, and_6_out};  // Bit_Extender bit_extender_6
  assign {and_8_out, RM_2, RN_2, RD_2} = bit_extender_5_out & Instru;  // AND_Gate and_8, 16 bits wide
  assign {and_9_out, IMM3, RN_3, RD_3} = bit_extender_6_out & Instru;  // AND_Gate and_9, 16 bits wide
  or or_8 (or_8_out, sub_imm, sub_reg);
  assign IMM8 = and_3_out[7:0] | and_7_out[7:0];  // OR_Gate or_9, 8 bits wide
  and and_10 (and_10_out, or_8_out, ADD_REG);
  or or_10 (Carry, and_10_out, SUB);
  assign bit_extender_7_out = {{24{1'b0}}, IMM8};  // Bit_Extender bit_extender_7
  not not_1 (not_1_out, Instru[13]);
  not not_2 (not_2_out, Instru[12]);
  not not_3 (not_3_out, Instru[11]);
  not not_4 (not_4_out, Instru[9]);
  assign bit_extender_8_out = {{29{1'b0}}, IMM3};  // Bit_Extender bit_extender_8
  Negator #(.width(32)) negator_1 (.in(bit_extender_7_out), .out(negator_1_out));
  and and_11 (and_11_out, not_1_out, Instru[11], not_4_out);
  Multiplexer #(.enable("false"), .width(32)) multiplexer_1 (
    .in0(bit_extender_7_out), .in1(negator_1_out), .out(multiplexer_1_out), .sel(MOV));
  and and_12 (and_12_out, not_3_out, Instru[13]);
  or or_11 (or_11_out[0], and_11_out, and_12_out, and_13_out);
  assign Imm32 = bit_extender_8_out | multiplexer_1_out;  // OR_Gate or_12, 32 bits wide
  and and_13 (and_13_out, Instru[11], not_2_out, not_1_out);
  assign bit_extender_9_out = {{3{Enable}}, Enable};  // Bit_Extender bit_extender_9
  Flag_Update flag_update_1 (.codop(Instru[13:11]), .flags_update_mask(flag_update_1_flags_update_mask));
  assign Rm = RM_t | RM_2;  // OR_Gate or_13, 3 bits wide
  assign Rn = RN_2 | RDN_4 | RM_t | RN_3;  // OR_Gate or_14, 3 bits wide
  assign Rd = RD_t | RD_3 | RD_2 | RD_4 | RDN_4;  // OR_Gate or_15, 3 bits wide
  and and_14 (and_14_out, Instru[13], Instru[11]);
  assign Flags_Update_Mask = bit_extender_9_out & flag_update_1_flags_update_mask;  // AND_Gate and_15, 4 bits wide
  and and_16 (and_16_out, Instru[9], Instru[11]);
  or or_16 (or_11_out[1], and_14_out, and_16_out, and_17_out);
  and and_17 (and_17_out, not_1_out, not_2_out);
  and and_18 (or_11_out[3], not_2_out, Instru[13]);
  assign bit_extender_10_out = {{3{Enable}}, Enable};  // Bit_Extender bit_extender_10
  assign ALU_Opcode = bit_extender_10_out & {or_11_out[3], Instru[12], or_11_out[1:0]};  // AND_Gate and_19, 4 bits wide

  // Notes on the sheet:
  //   Note 3: Imm32_Enable forces the use of the immediate for Rm register
  //   Note: ALU uses Rn register for shifts. Use Rn instead of Rm for shifts (immediate) here too
  //   Note 2: MOV uses RSB ALU opcode with Imm8 reversed so that it is copied to output register
  //   Pull output low on Enable = 0
  //   ALU will use Imm32 instead of Rm
  //   only ADD and SUB use Rm
  //   Enable carry for SUB since it is reversed in ALU
  //   ALU will use Imm32 instead of Rm
endmodule

module Flag_Update (
  input  [2:0] codop,
  output [3:0] flags_update_mask
);

  wire and_1_out, and_2_out, and_3_out, not_1_out;

  not not_1 (not_1_out, codop[2]);
  or or_1 (flags_update_mask[1], not_1_out, codop[0], codop[1]);
  and and_1 (and_1_out, codop[1], codop[0]);
  and and_2 (and_2_out, codop[2], codop[0]);
  and and_3 (and_3_out, codop[2], codop[1]);
  or or_2 (flags_update_mask[0], and_1_out, and_2_out, and_3_out);

  assign flags_update_mask[3:2] = 2'b11;
endmodule
